# Fritzing sketch preamp (saved by Fritzing 0.8.3b)
breadboards: 1

parts:
  IC1 = IC, DIP package, 8 pins [chip_label=IC]
  VCC1 = Battery block 9V
  R1 = Resistor [tolerance=±5% resistance=47k package=THT]
  R2 = Resistor [tolerance=±5% resistance=47k package=THT]
  TRS1 = Audio Jack (TRS) 3.5mm [package="4Ucon 08780 [THT]"]
  C1 = Tantalum Capacitor [capacitance=10µF voltage=16V package="100 mil [THT, tantalum]"]
  C2 = Tantalum Capacitor [capacitance=10µF voltage=16V package="100 mil [THT, tantalum]"]

nets:
  N1: IC1.pin1, C2.+
  N2: IC1.pin4, R1.Pin_1, R2.Pin_0
  N3: IC1.pin7, C1.+
  N4: VCC1.-, R2.Pin_1, TRS1.Sleeve
  N5: VCC1.+, R1.Pin_0
  N6: TRS1.Ring, C1.-
  N7: TRS1.Tip, C2.-
